# Fritzing sketch neje_laser_trigger (saved by Fritzing 0.9.3b)
circuit board: 4cm x 2cm
breadboards: 1

parts:
  TIP120_or_equivilent = npn-Powertransistor [package="TO220 [THT]"]
  R1 = Resistor [tolerance=±5% resistance=1k package=THT]
  SPNEN_pin_on_shield = female pin header, 1 pin [form="♀ (female)"]
  Power_Supply_negative/ground = female pin header, 1 pin [form="♀ (female)"]
  Laser_negative_(black_wire) = female pin header, 1 pin [form="♀ (female)"]

nets:
  N1: TIP120_or_equivilent.base, R1.Pin_1
  N2: TIP120_or_equivilent.collector, Power_Supply_negative/ground.pin1
  N3: TIP120_or_equivilent.emitter, Laser_negative_(black_wire).pin1
  N4: R1.Pin_0, SPNEN_pin_on_shield.pin1

notes:
  To SPNEN
  To Laser negative
  To Power Supply negative
